// Logisim project proc_RAM.circ as structural Verilog: 1 circuit, main circuit main
module main (
);

  wire cdm_8_mark5_1_p8, Cl, code, comparator_1_eq, data, data_ins_prime, memory, not_1_out, not_2_out,
       read_write_prime;
  wire [7:0] addr, cdm_8_mark5_1_p6, cdm_8_mark5_1_p7, D;

  // Debugger debugger_1: pin names not known
  Clock clock_1 (.out(Cl));
  not not_1 (not_1_out, data_ins_prime);
  Comparator comparator_1 (.a(addr), .b(8'hf0), .eq(comparator_1_eq));  // open: gt, lt
  // CdM_8_mark5 cdm_8_mark5_1: pin names not known; wires that end beside it: Cl, data_ins_prime, memory, read_write_prime, addr, cdm_8_mark5_1_p6, cdm_8_mark5_1_p7, cdm_8_mark5_1_p8
  and and_1 (cdm_8_mark5_1_p8, not_1_out, read_write_prime, memory, comparator_1_eq);
  assign D = not_2_out ? cdm_8_mark5_1_p6 : 8'bz;  // Controlled_Buffer controlled_buffer_1
  not not_2 (not_2_out, read_write_prime);
  assign cdm_8_mark5_1_p7 = read_write_prime ? D : 8'bz;  // Controlled_Buffer controlled_buffer_2
  Decoder decoder_1 (.out0(code), .out1(data), .sel(data_ins_prime), .en(memory));
  ROM rom_1 (.addr(addr), .data(D), .sel(code));
  RAM ram_1 (.addr(addr), .data(D), .sel(data), .clk(Cl), .ld(read_write_prime));  // open: clr

  // Notes on the sheet:
  //   contents of rom_1 (hex, n*v repeats v):
  //   d0 b0 88 c1 d1 9 a4 c5 cd 0 d0 f2 b0 0 e1 19 d0 f1 d1 0 a1 d6 1a ee a d4 d1 20 89 e0 2c d0 80 0 e0
  //   29 d6 3a 98 ee 21 20 ee 1c d7 d3 f0 bf f e1 37 d2 b0 ee 39 d2 d0 d7 d6 2d 16 ba 42 a e1 46 d2 0 ee
  //   48 d2 1 d7 d7
endmodule
